// Digital circuit UTS NO 3.dig as structural Verilog
module UTS_NO_3 (
  input  X,
  input  Y,
  input  Z,
  output Q
);

  wire and_1_out, not_1_out, not_3_out;

  not not_1 (not_1_out, Z);
  // Not not_2 has open pins: in=X, out=open
  and and_1 (and_1_out, X, Y);
  not not_3 (not_3_out, Y);
  // And and_2 has open pins: In_1=Y, In_2=not_1_out, out=open
  or or_1 (Q, and_1_out, not_3_out);

  // Notes on the sheet:
  //   Vega Rijki Perkasa
  //   x'y'z' + yz' + xy
endmodule
